# Fritzing sketch Circuit_Piezo_buzzer_BME280 (saved by Fritzing 0.9.3b)
breadboards: 1

parts:
  Composant1 = Arduino Mega 2560 (Rev3)
  Composant2 = BME280 Breakout
  J1 = Piezo Speaker
  Q1 = TRANSISTOR_NPN [package=to-92]

nets:
  N1: Composant1.D21/SCL, Composant2.SCK/SCL
  N2: Composant1.D20/SDA, Composant2.SDI/SDA
  N3: Composant1.D9_PWM, Q1.B
  3V3: Composant1.3V3, Composant2.3.3V, Q1.C
  GND: Composant1.GND, Composant2.GND, J1.pin1
  N4: J1.pin2, Q1.E
