# Fritzing sketch Global_no_lcd (saved by Fritzing 0.9.3b)
breadboards: 1

parts:
  Composant1 = BME280 Breakout
  Composant2 = BME280 Breakout
  Composant3 = Arduino Mega ADK (Rev3)
  Oxygen_sensor = Piezo Speaker
  Buzzer = Piezo Speaker
  U1 = LM 358 Dual Op-Amp [package="SO 08 [SMD]"]  # not connected
  Pneumatic_Motor = OMRON PCB Power Relay – G5LE [part_number="G5LE-1\n" package=THT]
  Expiration_Valve = OMRON PCB Power Relay – G5LE [part_number="G5LE-1\n" package=THT]
  R1 = Resistor [tolerance=±5% resistance=10 package="0603 [SMD]"]
  R2 = Resistor [tolerance=±5% resistance=510 package="0805 [SMD]"]
  U2 = TRANSISTOR_NPN_2 [package=to-92]

nets:
  GND: Composant1.GND, Composant2.GND, Composant3.GND, Oxygen_sensor.pin1, Buzzer.pin1, Pneumatic_Motor.COIL2, Expiration_Valve.COIL2, R1.Pin_0
  3.3V: Composant1.3.3V, Composant2.3.3V, Composant3.5V, U2.C
  N1: Composant1.SDI/SDA, Composant2.SDI/SDA, Composant3.D21/SCL
  N2: Composant1.SCK/SCL, Composant2.SCK/SCL, Composant3.D20/SDA
  N3: Composant3.A7, R2.Pin_1
  N4: Composant3.D2_PWM, U2.B
  N5: Composant3.D22, Pneumatic_Motor.COIL1
  N6: Composant3.D24, Expiration_Valve.COIL1
  N7: Buzzer.pin2, U2.E
  N8: R1.Pin_1, R2.Pin_0
