# Fritzing sketch alarme_pression (saved by Fritzing 0.9.3b)
breadboards: 1

parts:
  Composant1 = Arduino Mega 2560 (Rev3)
  Composant2 = BME280 Breakout
  J1 = Piezo Speaker

nets:
  N1: Composant1.D21/SCL, Composant2.SCK/SCL
  N2: Composant1.D20/SDA, Composant1.SDA, Composant2.SDI/SDA
  N3: Composant1.D9_PWM, J1.pin2
  3V3: Composant1.3V3, Composant2.3.3V
  GND: Composant1.GND, Composant2.GND, J1.pin1
