# Fritzing sketch Circuit_Oxygen_sensor (saved by Fritzing 0.9.3b)
breadboards: 1

parts:
  MCP6272 = Dual Op-Amp [package=dip08]
  Oxygen_Detector = Piezo Speaker
  R1 = Resistor [tolerance=±5% resistance=510 package=THT]
  R2 = Resistor [tolerance=±5% resistance=10 package=THT]
  Composant1 = Arduino Mega ADK (Rev3)

nets:
  N1: MCP6272.A_V-, Composant1.GND
  N2: MCP6272.B_+IN, R1.Pin_0, Composant1.A1
  N3: MCP6272.B_-IN, R1.Pin_1, R2.Pin_1
  N4: MCP6272.B_OUT, Oxygen_Detector.pin2
  N5: MCP6272.A_V+, Oxygen_Detector.pin1, R2.Pin_0, Composant1.5V
